// Logisim project tarfea-05.circ as structural Verilog: 1 circuit, main circuit main
module main (
  input  [3:0] ABCD,
  output a,
  output b,
  output c,
  output d,
  output e,
  output f,
  output g
);

  wire and_1_out, and_2_out, and_3_out, and_4_out, and_6_out, and_7_out, and_8_out, and_9_out, and_10_out,
       and_11_out, and_12_out, and_13_out, and_14_out, not_1_out, not_2_out, not_3_out, not_4_out;

  not not_1 (not_1_out, ABCD[3]);
  not not_2 (not_2_out, ABCD[2]);
  not not_3 (not_3_out, ABCD[1]);
  not not_4 (not_4_out, ABCD[0]);
  and and_1 (and_1_out, not_1_out, not_2_out, not_3_out, ABCD[0]);
  and and_2 (and_2_out, ABCD[2], not_3_out, not_4_out);
  and and_3 (and_3_out, ABCD[2], not_3_out, ABCD[0]);
  and and_4 (and_4_out, ABCD[2], ABCD[1], not_4_out);
  and and_5 (c, not_1_out, not_2_out, ABCD[1], not_4_out);
  and and_6 (and_6_out, not_1_out, not_2_out, not_3_out, ABCD[0]);
  and and_7 (and_7_out, ABCD[2], not_3_out, not_4_out);
  and and_8 (and_8_out, ABCD[2], ABCD[1], ABCD[0]);
  and and_9 (and_9_out, ABCD[2], not_3_out);
  and and_10 (and_10_out, not_1_out, not_2_out, ABCD[0]);
  and and_11 (and_11_out, not_1_out, not_2_out, ABCD[1]);
  and and_12 (and_12_out, ABCD[1], ABCD[0]);
  and and_13 (and_13_out, not_1_out, not_2_out, not_3_out);
  and and_14 (and_14_out, not_1_out, ABCD[2], ABCD[1], ABCD[0]);
  or or_1 (a, and_1_out, and_2_out);
  or or_2 (b, and_3_out, and_4_out);
  or or_3 (d, and_6_out, and_7_out, and_8_out);
  or or_4 (e, and_9_out, ABCD[0]);
  or or_5 (f, and_10_out, and_11_out, and_12_out);
  or or_6 (g, and_13_out, and_14_out);
  _7_Segment_Display #(.active("false")) u_7_segment_display_1 (
    .g(g), .f(f), .a(a), .b(b), .e(e), .d(d), .c(c));  // open: dp
endmodule
